# Fritzing sketch Lab 7 (saved by Fritzing 0.7.10b)
breadboards: 1

parts:
  Arduino1 = Arduino
  R1 = Resistor [tolerance=±0.25% resistance=330 package=THT]
  S1 = Pushbutton [package="[THT]"]
  LED1 = LED - 5mm [color="Green (555nm)" package="5 mm [THT]"]
  R2 = Resistor [tolerance=±5% resistance=10k package=THT]

nets:
  N1: Arduino1.GND, LED1.cathode, R2.Pin_0
  N2: Arduino1.D12, R1.Pin_1
  N3: Arduino1.D7, S1.Pin_1, S1.Pin_2, R2.Pin_1
  N4: Arduino1.+5V, S1.Pin_3, S1.Pin_4
  N5: R1.Pin_0, LED1.anode
