# Fritzing sketch Elevator (saved by Fritzing 0.7.10b)
breadboards: 1

parts:
  Arduino1 = Arduino
  LED1 = LED - 5mm [color="Red (633nm)" package="5 mm [THT]"]
  LED2 = LED - 5mm [color="Red (633nm)" package="5 mm [THT]"]
  LED3 = LED - 5mm [color="Red (633nm)" package="5 mm [THT]"]
  LED4 = LED - 5mm [color="Green (555nm)" package="5 mm [THT]"]
  LED5 = LED - 5mm [color="Red (633nm)" package="5 mm [THT]"]
  S1 = Pushbutton [package="[THT]"]
  S2 = Pushbutton [package="[THT]"]
  R1 = Resistor [tolerance=±5% resistance=330 package=THT]
  R2 = Resistor [tolerance=±5% resistance=330 package=THT]
  R3 = Resistor [tolerance=±5% resistance=330 package=THT]
  R4 = Resistor [tolerance=±5% resistance=330 package=THT]
  R5 = Resistor [tolerance=±5% resistance=330 package=THT]
  R6 = Resistor [tolerance=±5% resistance=10k package=THT]
  R7 = Resistor [tolerance=±5% resistance=10k package=THT]
  J1 = Piezo Speaker

nets:
  N1: Arduino1.GND, LED1.cathode, LED2.cathode, LED3.cathode, LED4.cathode, LED5.cathode, R6.Pin_1, R7.Pin_1, J1.pin1
  N2: Arduino1.D12, LED2.anode, R5.Pin_0, R5.Pin_1
  N3: Arduino1.D11, LED3.anode, R2.Pin_0, R2.Pin_1
  N4: Arduino1.D10, LED4.anode, R4.Pin_0, R4.Pin_1
  N5: Arduino1.D9, LED1.anode, R3.Pin_0, R3.Pin_1
  N6: Arduino1.D8, LED5.anode, R1.Pin_0, R1.Pin_1
  N7: Arduino1.D7, S1.Pin_1, S1.Pin_2, R6.Pin_0
  N8: Arduino1.D6, S2.Pin_1, S2.Pin_2, R7.Pin_0
  N9: Arduino1.D5, J1.pin2
  N10: S1.Pin_3, S1.Pin_4
  N11: S2.Pin_3, S2.Pin_4
