# Fritzing sketch Laser (saved by Fritzing 0.7.10b)
breadboards: 1

parts:
  Arduino1 = Arduino
  LED1 = green LED - 5mm
  LED2 = green LED - 5mm
  LED3 = green LED - 5mm
  S1 = Pushbutton [package="[SMD]"]
  LED5 = Red LED - 5mm [package="5 mm [THT]"]
  R1 = Resistor [tolerance=±5% resistance=330 package=THT]
  R2 = Resistor [tolerance=±5% resistance=330 package=THT]
  R3 = Resistor [tolerance=±5% resistance=330 package=THT]
  R5 = Resistor [tolerance=±5% resistance=330 package=THT]
  R6 = Resistor [tolerance=±5% resistance=330 package=THT]
  R7 = Resistor [tolerance=±5% resistance=10k package=THT]
  LED6 = green LED - 5mm

nets:
  N1: Arduino1.GND, LED1.cathode, LED2.cathode, LED3.cathode, LED5.cathode, R7.Pin_0, LED6.cathode
  N2: Arduino1.D12, R2.Pin_1
  N3: Arduino1.D11, R3.Pin_1
  N4: Arduino1.D10, R6.Pin_1
  N5: Arduino1.D9, R5.Pin_1
  N6: Arduino1.D8, R1.Pin_1
  N7: Arduino1.D7, S1.Pin_1, S1.Pin_2, R7.Pin_1
  N8: Arduino1.+5V, S1.Pin_3, S1.Pin_4
  N9: LED1.anode, R6.Pin_0
  N10: LED2.anode, R5.Pin_0
  N11: LED3.anode, R1.Pin_0
  N12: LED5.anode, R2.Pin_0
  N13: R3.Pin_0, LED6.anode
