# Fritzing sketch Police Lights Fritzing (saved by Fritzing 0.7.10b)
breadboards: 1

parts:
  Arduino1 = Arduino
  LED2 = LED - 5mm [color="Red (633nm)" package="5 mm [THT]"]
  R1 = 330 Ω Resistor [package=THT]
  R2 = 330 Ω Resistor [package=THT]
  LED3 = Blue LED - 5mm [package="5 mm [THT]"]

nets:
  N1: Arduino1.GND, LED2.cathode, LED3.cathode
  N2: Arduino1.D11, R2.Pin_1
  N3: LED2.anode, R1.Pin_0
  N4: R2.Pin_0, LED3.anode
