# Fritzing sketch Button (saved by Fritzing 0.7.10b)
breadboards: 1

parts:
  Arduino1 = Arduino
  LED1 = LED - 5mm [color="Red (633nm)" package="5 mm [THT]"]
  S1 = Pushbutton [package="[SMD]"]
  R1 = 330 Ω Resistor [package=THT]
  R2 = 10k Ω Resistor [package=THT]

nets:
  N1: Arduino1.GND, LED1.cathode
  N2: Arduino1.D12, R1.Pin_1
  N3: Arduino1.D7, S1.Pin_1, S1.Pin_2, R2.Pin_1
  N4: LED1.anode, R1.Pin_0
  N5: S1.Pin_3, S1.Pin_4
